// Logisim project Binary to Gray convertor.circ as structural Verilog: 1 circuit, main circuit main
module main (
  input  B0,
  input  B1,
  input  B2,
  input  B3,
  output G0,
  output G1,
  output G2,
  output G3
);

  xor xor_1 (G0, B0, B1);
  xor xor_2 (G1, B1, B2);
  xor xor_3 (G2, B2, B3);

  assign G3 = B3;
endmodule
