// Logisim project DEMUX 1BIT.circ as structural Verilog: 1 circuit, main circuit main
module main (
  input  in_1,
  input  in_2
);

  wire demultiplexer_1_out0, demultiplexer_1_out1;

  Demultiplexer demultiplexer_1 (
    .out0(demultiplexer_1_out0), .out1(demultiplexer_1_out1), .in(in_1), .sel(in_2));  // open: en
  LED Y0 (.in(demultiplexer_1_out0));
  LED Y1 (.in(demultiplexer_1_out1));
endmodule
