// Logisim project DEMUX 2BIT.circ as structural Verilog: 1 circuit, main circuit main
module main (
  input  in_1,
  input  [1:0] in_2
);

  wire demultiplexer_1_out0, demultiplexer_1_out1, demultiplexer_1_out2, demultiplexer_1_out3;

  Demultiplexer #(.select(2)) demultiplexer_1 (
    .out0(demultiplexer_1_out0), .out1(demultiplexer_1_out1), .out2(demultiplexer_1_out2),
    .out3(demultiplexer_1_out3), .in(in_1), .sel(in_2));  // open: en
  LED Y0 (.in(demultiplexer_1_out0));
  LED Y1 (.in(demultiplexer_1_out1));
  LED Y2 (.in(demultiplexer_1_out2));
  LED Y3 (.in(demultiplexer_1_out3));
endmodule
