// Logisim project MUX 1BIT.circ as structural Verilog: 1 circuit, main circuit main
module main (
  input  I0,
  input  I1,
  input  S
);

  wire multiplexer_1_out;

  Multiplexer multiplexer_1 (.in0(I0), .in1(I1), .out(multiplexer_1_out), .sel(S));  // open: en
  LED led_1 (.in(multiplexer_1_out));
endmodule
