// Logisim project MUX 4BIT.circ as structural Verilog: 1 circuit, main circuit main
module main (
  input  I0,
  input  I1,
  input  I2,
  input  I3,
  input  I4,
  input  I5,
  input  I6,
  input  I7,
  input  I8,
  input  I9,
  input  I10,
  input  I11,
  input  I12,
  input  I13,
  input  I14,
  input  [3:0] in_16,
  input  I15
);

  wire multiplexer_1_out;

  Multiplexer #(.select(4)) multiplexer_1 (
    .in0(I0), .in1(I1), .in2(I2), .in3(I3), .in4(I4), .in5(I5), .in6(I6), .in7(I7), .in8(I8), .in9(I9),
    .in10(I10), .in11(I11), .in12(I12), .in13(I13), .in14(I14), .in15(I15), .out(multiplexer_1_out),
    .sel(in_16));  // open: en
  LED led_1 (.in(multiplexer_1_out));
endmodule
