// Logisim project NAND, NOR gats.circ as structural Verilog: 1 circuit, main circuit main
module main (
  input  in_1,
  input  in_2,
  input  in_3,
  input  in_4,
  input  in_5,
  input  in_6,
  input  in_7,
  input  in_8,
  input  in_9,
  input  in_10,
  input  in_11,
  input  in_12,
  output out_13,
  output out_14,
  output out_15,
  output out_16,
  output out_17,
  output out_18
);

  wire nand_2_out, nand_3_out, nand_4_out, nor_1_out, nor_2_out, nor_3_out;

  nand nand_1 (out_14, in_2, in_2);
  nand nand_2 (nand_2_out, in_4, in_6);
  nand nand_3 (nand_3_out, in_8, in_10);
  nand nand_4 (nand_4_out, in_10, in_12);
  nand nand_5 (out_18, nand_3_out, nand_4_out);
  nand nand_6 (out_16, nand_2_out, nand_2_out);
  nor nor_1 (nor_1_out, in_7, in_9);
  nor nor_2 (nor_2_out, in_9, in_11);
  nor nor_3 (nor_3_out, in_3, in_5);
  nor nor_4 (out_13, in_1, in_1);
  nor nor_5 (out_17, nor_1_out, nor_2_out);
  nor nor_6 (out_15, nor_3_out, nor_3_out);
endmodule
