// Logisim project Priority Encoder 2 BIT.circ as structural Verilog: 1 circuit, main circuit main
module main (
  input  in_1,
  input  in_2,
  input  [1:0] in_3,
  input  in_4,
  input  in_5,
  input  in_6
);

  Priority_Encoder #(.select(2)) priority_encoder_1 (
    .in0(in_1), .in1(in_2), .in2(in_4), .in3(in_6), .out(in_3), .en_in(in_5));  // open: gs, en_out
endmodule
