// Logisim project Priority Encoder 3 BIT.circ as structural Verilog: 1 circuit, main circuit main
module main (
  input  _0,
  input  _1,
  input  _2,
  input  _3,
  input  [2:0] in_5,
  input  _4,
  input  _5,
  input  _6,
  input  _7,
  input  in_10
);

  Priority_Encoder priority_encoder_1 (
    .in0(_0), .in1(_1), .in2(_2), .in3(_3), .in4(_4), .in5(_5), .in6(_6), .in7(_7), .out(in_5), .en_in(in_10));  // open: gs, en_out
endmodule
