// Logisim project Problem 4.circ as structural Verilog: 1 circuit, main circuit main
module main (
  input  in_1,
  input  in_2,
  input  in_3
);

  wire and_1_out, and_2_out, not_1_out, not_2_out, or_1_out;

  not not_1 (not_1_out, in_2);
  not not_2 (not_2_out, in_2);
  and and_1 (and_1_out, in_1, in_2, in_3);
  or or_1 (or_1_out, not_1_out, not_2_out);
  and and_2 (and_2_out, in_1, or_1_out);
  // OR_Gate or_2 has open pins: in0=and_1_out, in1=and_2_out, out=open
endmodule
