// Logisim project Problem 6.circ as structural Verilog: 1 circuit, main circuit main
module main (
  input  A,
  input  B,
  input  C,
  output Y
);

  wire D_A_B_out, E_A_C_out, F_A_B_C_out;

  and D_A_B (D_A_B_out, A, B);
  and E_A_C (E_A_C_out, A, C);
  and F_A_B_C (F_A_B_C_out, A, B, C);
  or or_1 (Y, D_A_B_out, E_A_C_out, F_A_B_C_out);
endmodule
