// Logisim project Problem 7.circ as structural Verilog: 1 circuit, main circuit main
module main (
  input  A,
  input  B,
  input  C,
  output Y
);

  wire nand_1_out, nand_2_out, not_1_out;

  not not_1 (not_1_out, A);
  nand nand_1 (nand_1_out, A, B);
  nand nand_2 (nand_2_out, not_1_out, C);
  nand nand_3 (Y, nand_1_out, nand_2_out);
endmodule
