// Logisim project XNOR Gate.circ as structural Verilog: 1 circuit, main circuit main
module main (
  input  in_1,
  input  in_2,
  output out_3
);

  xnor xnor_1 (out_3, in_1, in_2);

  // Notes on the sheet:
  //   XNOR GATE
endmodule
